// Logisim project Projectv12345(1).circ as structural Verilog: 5 circuits, main circuit main
module main (
  input  E,
  input  X,
  input  Reset,
  output [5:0] State_n,
  output [5:0] State
);

  wire CLK_out, light_1_g, light_1_r, light_1_y, light_2_g, light_2_r, light_2_y, seven_segment_1_a,
       seven_segment_1_b, seven_segment_1_c, seven_segment_1_d, seven_segment_1_e, seven_segment_1_f,
       seven_segment_1_g, state_outputs_1_c_0, state_outputs_1_c_1, state_outputs_1_c_2, state_outputs_1_c_3,
       state_outputs_1_le_0, state_outputs_1_le_1, state_outputs_1_lx_0, state_outputs_1_lx_1;

  StateTransitions statetransitions_1 (.State(State), .E(E), .X(X), .State_n(State_n));
  Clock CLK (.out(CLK_out));
  Register #(.width(6)) register_1 (.D(State_n), .clk(CLK_out), .Q(State), .clr(Reset));  // open: en
  State_Outputs state_outputs_1 (
    .State(State), .LE_1(state_outputs_1_le_1), .LE_0(state_outputs_1_le_0), .LX_1(state_outputs_1_lx_1),
    .LX_0(state_outputs_1_lx_0), .C_3(state_outputs_1_c_3), .C_2(state_outputs_1_c_2),
    .C_1(state_outputs_1_c_1), .C_0(state_outputs_1_c_0));
  Seven_Segment seven_segment_1 (
    .C_0(state_outputs_1_c_0), .C_1(state_outputs_1_c_1), .C_2(state_outputs_1_c_2),
    .C_3(state_outputs_1_c_3), .A(seven_segment_1_a), .B(seven_segment_1_b), .C(seven_segment_1_c),
    .D(seven_segment_1_d), .E(seven_segment_1_e), .F(seven_segment_1_f), .G(seven_segment_1_g));
  Light light_1 (.L_1(state_outputs_1_le_1), .L_0(state_outputs_1_le_0), .G(light_1_g), .Y(light_1_y), .R(light_1_r));
  Light light_2 (.L_1(state_outputs_1_lx_1), .L_0(state_outputs_1_lx_0), .G(light_2_g), .Y(light_2_y), .R(light_2_r));
  _7_Segment_Display u_7_segment_display_1 (
    .g(seven_segment_1_g), .f(seven_segment_1_f), .a(seven_segment_1_a), .b(seven_segment_1_b),
    .e(seven_segment_1_e), .d(seven_segment_1_d), .c(seven_segment_1_c));  // open: dp
  LED G_E (.in(light_1_g));
  LED Y_E (.in(light_1_y));
  LED R_E (.in(light_1_r));
  LED G_X (.in(light_2_g));
  LED Y_X (.in(light_2_y));
  LED R_X (.in(light_2_r));
endmodule

module Light (
  input  L_1,
  input  L_0,
  output G,
  output Y,
  output R
);

  wire not_1_out, not_2_out;

  not not_1 (not_1_out, L_0);
  not not_2 (not_2_out, L_1);
  and and_1 (G, not_1_out, not_2_out);
  and and_2 (Y, not_2_out, L_0);
  and and_3 (R, L_1, not_1_out);
endmodule

module State_Outputs (
  input  [5:0] State,
  output LE_1,
  output LE_0,
  output LX_1,
  output LX_0,
  output C_3,
  output C_2,
  output C_1,
  output C_0
);

  wire and_1_out, and_2_out, and_3_out, and_4_out, and_5_out, and_6_out, and_7_out, and_8_out, and_9_out,
       and_10_out, and_11_out, and_12_out, and_13_out, and_14_out, and_15_out, and_16_out, and_17_out,
       and_18_out, and_19_out, and_20_out, and_21_out, and_22_out, and_23_out, and_24_out, and_25_out,
       and_26_out, and_27_out, and_28_out, and_29_out, and_30_out, and_31_out, and_32_out, and_33_out,
       and_34_out, and_35_out, and_36_out, and_37_out, and_38_out, not_1_out, not_2_out, not_3_out,
       not_4_out, not_5_out, not_6_out;

  not not_1 (not_1_out, State[5]);
  not not_2 (not_2_out, State[4]);
  not not_3 (not_3_out, State[3]);
  not not_4 (not_4_out, State[2]);
  not not_5 (not_5_out, State[1]);
  not not_6 (not_6_out, State[0]);
  and and_1 (and_1_out, State[5], not_5_out);
  and and_2 (and_2_out, not_1_out, not_2_out, State[3], not_4_out, State[1], not_6_out);
  and and_3 (and_3_out, State[3], State[2], not_5_out);
  and and_4 (and_4_out, State[4], not_5_out);
  and and_5 (and_5_out, State[4], State[1], State[0]);
  and and_6 (and_6_out, State[5], State[1], State[0]);
  and and_7 (and_7_out, State[3], State[1], State[0]);
  and and_8 (and_8_out, not_1_out, not_2_out, not_3_out);
  and and_9 (and_9_out, not_1_out, not_2_out, not_4_out, not_5_out);
  and and_10 (and_10_out, State[2], State[1]);
  and and_11 (and_11_out, State[4], State[1]);
  and and_12 (and_12_out, State[5], State[1]);
  and and_13 (and_13_out, not_1_out, not_2_out, not_4_out, State[0]);
  and and_14 (and_14_out, State[4], not_5_out, State[0]);
  and and_15 (and_15_out, State[5], not_5_out, State[0]);
  and and_16 (and_16_out, not_1_out, not_2_out, State[3], not_4_out, State[1], not_6_out);
  and and_17 (and_17_out, State[3], State[2], not_5_out, State[0]);
  and and_18 (and_18_out, State[5], State[2], State[1], State[0]);
  and and_19 (and_19_out, not_2_out, State[3], not_4_out, not_5_out);
  and and_20 (and_20_out, State[5], State[3]);
  and and_21 (and_21_out, State[5], not_3_out, not_4_out);
  and and_22 (and_22_out, State[4], State[3]);
  and and_23 (and_23_out, not_2_out, not_3_out, State[2], not_5_out);
  and and_24 (and_24_out, not_2_out, not_3_out, State[2], not_6_out);
  and and_25 (and_25_out, not_1_out, not_3_out, State[2], State[1], State[0]);
  and and_26 (and_26_out, State[4], not_3_out, not_5_out);
  and and_27 (and_27_out, State[3], State[2], State[1], State[0]);
  and and_28 (and_28_out, State[5], not_3_out, not_5_out);
  and and_29 (and_29_out, not_1_out, not_2_out, not_3_out, State[1]);
  and and_30 (and_30_out, not_3_out, not_4_out, State[1]);
  and and_31 (and_31_out, not_3_out, State[1], not_6_out);
  and and_32 (and_32_out, not_4_out, State[1], State[0]);
  and and_33 (and_33_out, State[5], State[2], not_6_out);
  and and_34 (and_34_out, not_1_out, not_2_out, not_3_out, State[0]);
  and and_35 (and_35_out, State[3], State[2], not_6_out);
  and and_36 (and_36_out, State[4], State[2], not_6_out);
  and and_37 (and_37_out, State[2], not_5_out, State[0]);
  and and_38 (and_38_out, not_1_out, not_2_out, not_5_out, State[0]);
  or or_1 (LE_1, and_1_out, and_2_out, and_3_out, and_4_out);
  or or_2 (LE_0, and_5_out, and_6_out, and_7_out);
  or or_3 (LX_1, and_8_out, and_9_out, and_10_out, and_11_out, and_12_out, and_13_out);
  or or_4 (LX_0, and_14_out, and_15_out, and_16_out, and_17_out);
  or or_5 (C_3, and_18_out, and_19_out, and_20_out);
  or or_6 (C_2, and_21_out, and_22_out, and_23_out, and_24_out, and_25_out);
  or or_7 (C_1, and_26_out, and_27_out, and_28_out, and_29_out, and_30_out, and_31_out);
  or or_8 (C_0, and_32_out, and_33_out, and_34_out, and_35_out, and_36_out, and_37_out, and_38_out);
endmodule

module Seven_Segment (
  input  C_0,
  input  C_1,
  input  C_2,
  input  C_3,
  output A,
  output B,
  output C,
  output D,
  output E,
  output F,
  output G
);

  wire and_1_out, and_2_out, and_3_out, and_4_out, and_5_out, and_6_out, and_7_out, and_8_out, and_9_out,
       and_10_out, and_11_out, and_12_out, and_13_out, and_14_out, and_15_out, and_16_out, and_17_out,
       and_18_out, and_19_out, and_20_out, and_21_out, and_22_out, and_23_out, and_24_out, and_25_out,
       and_26_out, not_1_out, not_2_out, not_3_out, not_4_out;

  not not_1 (not_1_out, C_3);
  not not_2 (not_2_out, C_2);
  not not_3 (not_3_out, C_1);
  not not_4 (not_4_out, C_0);
  and and_1 (and_1_out, not_1_out, C_1);
  and and_2 (and_2_out, not_1_out, C_2, C_0);
  and and_3 (and_3_out, C_3, not_2_out, not_3_out);
  and and_4 (and_4_out, not_2_out, not_3_out, not_4_out);
  and and_5 (and_5_out, not_1_out, not_2_out);
  and and_6 (and_6_out, not_2_out, not_3_out);
  and and_7 (and_7_out, not_1_out, C_1, C_0);
  and and_8 (and_8_out, not_1_out, not_3_out, not_4_out);
  and and_9 (and_9_out, not_1_out, C_0);
  and and_10 (and_10_out, not_1_out, C_2);
  and and_11 (and_11_out, not_2_out, not_3_out);
  and and_12 (and_12_out, not_1_out, C_2, not_3_out, C_0);
  and and_13 (and_13_out, not_2_out, not_3_out, not_4_out);
  and and_14 (and_14_out, not_1_out, not_2_out, C_1);
  and and_15 (and_15_out, not_1_out, C_1, not_4_out);
  and and_16 (and_16_out, C_3, not_2_out, not_3_out);
  and and_17 (and_17_out, not_1_out, C_1, not_4_out);
  and and_18 (and_18_out, not_2_out, not_3_out, not_4_out);
  and and_19 (and_19_out, not_1_out, C_2, not_4_out);
  and and_20 (and_20_out, C_3, not_2_out, not_3_out);
  and and_21 (and_21_out, not_1_out, C_2, not_3_out);
  and and_22 (and_22_out, not_2_out, not_3_out, not_4_out);
  and and_23 (and_23_out, not_1_out, C_2, not_3_out);
  and and_24 (and_24_out, not_1_out, C_2, not_4_out);
  and and_25 (and_25_out, not_1_out, not_2_out, C_1);
  and and_26 (and_26_out, C_3, not_2_out, not_3_out);
  or or_1 (A, and_1_out, and_2_out, and_3_out, and_4_out);
  or or_2 (B, and_5_out, and_6_out, and_7_out, and_8_out);
  or or_3 (C, and_9_out, and_10_out, and_11_out);
  or or_4 (D, and_12_out, and_13_out, and_14_out, and_15_out, and_16_out);
  or or_5 (E, and_17_out, and_18_out);
  or or_6 (F, and_19_out, and_20_out, and_21_out, and_22_out);
  or or_7 (G, and_23_out, and_24_out, and_25_out, and_26_out);

  // Notes on the sheet:
  //   0
endmodule

module StateTransitions (
  input  [5:0] State,
  input  E,
  input  X,
  output [5:0] State_n
);

  wire and_1_out, and_2_out, and_3_out, and_4_out, and_5_out, and_6_out, and_7_out, and_8_out, and_9_out,
       and_10_out, and_11_out, and_12_out, and_13_out, and_14_out, and_15_out, and_16_out, and_17_out,
       and_18_out, and_19_out, and_20_out, and_21_out, and_22_out, and_23_out, and_24_out, and_25_out,
       and_26_out, and_27_out, and_28_out, and_29_out, and_30_out, and_31_out, and_32_out, and_33_out,
       and_34_out, and_35_out, and_36_out, and_37_out, and_38_out, and_39_out, and_40_out, and_41_out,
       and_42_out, and_43_out, and_44_out, and_45_out, and_46_out, and_47_out, and_48_out, and_49_out,
       and_50_out, and_51_out, and_52_out, and_53_out, and_54_out, and_55_out, and_56_out, and_57_out,
       and_58_out, and_59_out, and_60_out, and_61_out, and_62_out, and_63_out, and_64_out, and_65_out,
       and_66_out, and_67_out, and_68_out, and_69_out, and_70_out, and_71_out, not_1_out, not_2_out,
       not_3_out, not_4_out, not_5_out, not_6_out, not_7_out, not_8_out;

  not not_1 (not_1_out, State[5]);
  not not_2 (not_2_out, State[4]);
  not not_3 (not_3_out, State[3]);
  not not_4 (not_4_out, State[2]);
  not not_5 (not_5_out, State[1]);
  not not_6 (not_6_out, State[0]);
  not not_7 (not_7_out, E);
  not not_8 (not_8_out, X);
  and and_1 (and_1_out, State[5], not_5_out, not_8_out);
  and and_2 (and_2_out, State[5], State[0]);
  and and_3 (and_3_out, State[5], State[2], not_5_out);
  and and_4 (and_4_out, not_2_out, not_3_out, State[2], State[1], State[0], X);
  and and_5 (and_5_out, not_2_out, State[3], not_4_out, not_5_out, X);
  and and_6 (and_6_out, not_2_out, State[3], not_4_out, not_5_out, State[0]);
  and and_7 (and_7_out, State[4], State[3], State[2], State[1], State[0]);
  and and_8 (and_8_out, State[5], not_3_out, not_4_out, not_5_out, not_6_out, X);
  and and_9 (and_9_out, not_1_out, not_3_out, not_4_out, State[1], State[0], X);
  and and_10 (and_10_out, not_1_out, not_3_out, State[2], not_5_out, X);
  and and_11 (and_11_out, not_1_out, not_2_out, not_3_out, State[2], not_6_out, X);
  and and_12 (and_12_out, not_2_out, State[3], State[2], State[1], State[0]);
  and and_13 (and_13_out, State[4], not_5_out, not_8_out);
  and and_14 (and_14_out, State[4], not_3_out, State[0]);
  and and_15 (and_15_out, State[4], State[3], not_5_out);
  and and_16 (and_16_out, State[4], not_4_out, State[0]);
  and and_17 (and_17_out, State[5], not_3_out, not_4_out, not_5_out, not_6_out, X);
  and and_18 (and_18_out, not_1_out, not_2_out, not_5_out, State[0], X);
  and and_19 (and_19_out, not_1_out, not_2_out, not_3_out, State[1], not_6_out, X);
  and and_20 (and_20_out, State[5], State[2], State[1], E);
  and and_21 (and_21_out, State[5], State[2], State[1], State[0]);
  and and_22 (and_22_out, not_3_out, State[2], State[1], State[0], E, not_8_out);
  and and_23 (and_23_out, State[3], not_5_out, not_8_out);
  and and_24 (and_24_out, State[5], State[3], State[1]);
  and and_25 (and_25_out, State[3], not_4_out, State[0]);
  and and_26 (and_26_out, State[3], State[2], not_5_out);
  and and_27 (and_27_out, State[4], not_3_out, not_4_out, not_5_out, not_6_out, X);
  and and_28 (and_28_out, State[4], not_3_out, State[2], State[1], State[0]);
  and and_29 (and_29_out, not_2_out, not_3_out, State[1], not_6_out, X);
  and and_30 (and_30_out, State[5], not_3_out, not_4_out, State[1]);
  and and_31 (and_31_out, not_4_out, State[1], State[0], E, not_8_out);
  and and_32 (and_32_out, not_1_out, not_2_out, not_3_out, State[2], not_6_out);
  and and_33 (and_33_out, State[2], not_5_out, not_8_out);
  and and_34 (and_34_out, State[5], State[2], not_5_out, State[0]);
  and and_35 (and_35_out, not_1_out, not_2_out, not_3_out, State[2], not_7_out, not_8_out);
  and and_36 (and_36_out, State[3], not_4_out, not_5_out, not_6_out, X);
  and and_37 (and_37_out, State[3], not_4_out, State[1], State[0]);
  and and_38 (and_38_out, State[3], State[2], not_5_out, State[0]);
  and and_39 (and_39_out, State[4], not_4_out, not_5_out, not_6_out, X);
  and and_40 (and_40_out, State[4], not_4_out, State[1], State[0]);
  and and_41 (and_41_out, State[4], State[2], not_5_out, State[0]);
  and and_42 (and_42_out, State[4], State[3], State[1], not_6_out);
  and and_43 (and_43_out, State[5], not_3_out, not_4_out, not_6_out, X);
  and and_44 (and_44_out, not_2_out, not_3_out, State[2], not_6_out, not_7_out, not_8_out);
  and and_45 (and_45_out, not_1_out, not_3_out, State[2], not_6_out, E, not_8_out);
  and and_46 (and_46_out, State[5], not_5_out, State[0]);
  and and_47 (and_47_out, not_5_out, State[0], E);
  and and_48 (and_48_out, not_3_out, not_4_out, State[1], not_6_out);
  and and_49 (and_49_out, not_1_out, not_2_out, not_3_out, State[1], not_7_out);
  and and_50 (and_50_out, not_1_out, not_2_out, State[3], not_5_out, X);
  and and_51 (and_51_out, State[3], not_5_out, State[0]);
  and and_52 (and_52_out, State[4], not_5_out, State[0]);
  and and_53 (and_53_out, not_3_out, State[1], not_6_out, not_7_out);
  and and_54 (and_54_out, State[3], State[2], State[1], not_6_out, E);
  and and_55 (and_55_out, not_1_out, not_2_out, not_3_out, State[0], X);
  and and_56 (and_56_out, not_1_out, not_2_out, not_3_out, State[2], X);
  and and_57 (and_57_out, not_1_out, not_2_out, State[2], State[1], not_6_out, E);
  and and_58 (and_58_out, not_1_out, not_2_out, not_3_out, State[1], X);
  and and_59 (and_59_out, not_1_out, not_2_out, not_3_out, State[0], not_7_out);
  and and_60 (and_60_out, not_1_out, not_2_out, not_3_out, State[2], X);
  and and_61 (and_61_out, not_3_out, not_5_out, not_6_out, E, not_8_out);
  and and_62 (and_62_out, State[5], State[2], State[1], not_6_out, not_7_out);
  and and_63 (and_63_out, not_1_out, not_2_out, not_3_out, not_6_out, E);
  and and_64 (and_64_out, not_1_out, not_2_out, State[3], not_4_out, not_5_out, X);
  and and_65 (and_65_out, not_1_out, not_5_out, not_6_out, E, not_8_out);
  and and_66 (and_66_out, State[3], State[2], State[1], not_6_out, not_7_out);
  and and_67 (and_67_out, State[4], State[2], State[1], not_6_out, not_7_out);
  and and_68 (and_68_out, State[5], not_4_out, not_6_out, E, not_8_out);
  and and_69 (and_69_out, not_1_out, not_2_out, State[3], not_4_out, not_5_out, State[0]);
  and and_70 (and_70_out, not_1_out, not_2_out, not_3_out, E, X);
  and and_71 (and_71_out, State[4], not_4_out, not_6_out, E, not_8_out);
  or or_1 (State_n[5], and_1_out, and_2_out, and_3_out, and_4_out, and_5_out, and_6_out, and_7_out);
  or or_2 (State_n[4], and_8_out, and_9_out, and_10_out, and_11_out, and_12_out, and_13_out, and_14_out, and_15_out, and_16_out);
  or or_3 (State_n[3], and_17_out, and_18_out, and_19_out, and_20_out, and_21_out, and_22_out, and_23_out, and_24_out, and_25_out, and_26_out, and_27_out, and_28_out);
  or or_4 (State_n[2], and_29_out, and_30_out, and_31_out, and_32_out, and_33_out, and_34_out, and_35_out, and_36_out, and_37_out, and_38_out, and_39_out, and_40_out, and_41_out, and_42_out, and_43_out, and_44_out, and_45_out);
  or or_5 (State_n[1], and_46_out, and_47_out, and_48_out, and_49_out, and_50_out, and_51_out, and_52_out, and_53_out, and_54_out, and_55_out, and_56_out, and_57_out);
  or or_6 (State_n[0], and_58_out, and_59_out, and_60_out, and_61_out, and_62_out, and_63_out, and_64_out, and_65_out, and_66_out, and_67_out, and_68_out, and_69_out, and_70_out, and_71_out);
endmodule
